# Fritzing sketch ESPHome Wiegand3 (saved by Fritzing 1.0.4)
circuit board: 11cm x 7cm
breadboards: 1

parts:
  L7805CV = Voltage Regulator [package=78xxl]
  C1 = Electrolytic Capacitor [capacitance=0.47mF voltage=20V package="100 mil [THT, electrolytic]"]
  LED1 = LED - 5mm [color="Red (633nm)" current=0.030A package="5 mm [THT]"]
  R1 = Resistor [tolerance=±5% power=0.25W resistance=150 package=THT]
  W2812B = ws2812b [package="smd 2812b"]
  WeMos_D1_Mini1 = WeMos D1 Mini
  Active_Buzzer = Piezo Buzzer
  J1 = screw terminal, 2 pins
  J2 = screw terminal, 7 pins
  HLK-5M12 = HLK-5M05
  C2 = Electrolytic Capacitor [capacitance=0.47mF voltage=16V package="100 mil [THT, electrolytic]"]

nets:
  GND: L7805CV.GND, C1.-, LED1.cathode, W2812B.VSS, WeMos_D1_Mini1.G, Active_Buzzer.pin_1, J2.pin1, J2.pin6, HLK-5M12.-Vo, C2.-
  N1: L7805CV.IN, C1.+, J2.pin7, HLK-5M12.+Vo
  VDD: L7805CV.OUT, R1.Pin_0, W2812B.VDD, WeMos_D1_Mini1.5V, C2.+
  N2: LED1.anode, R1.Pin_1
  N3: W2812B.DIN, WeMos_D1_Mini1.D4
  N4: WeMos_D1_Mini1.D1, J2.pin5
  N5: WeMos_D1_Mini1.D2, J2.pin4
  N6: WeMos_D1_Mini1.D6, J2.pin3
  N7: WeMos_D1_Mini1.D7, Active_Buzzer.pin_2, J2.pin2
  N8: J1.pin1, HLK-5M12.pin_2
  N9: J1.pin2, HLK-5M12.pin_1

notes:
  +12
  GND
  D1
  D0
  OPEN
  SPK
  ESPHome Wiegand Controler
  S20-ID keypad and tag reader
  Fuse

custom parts:
  Piezo Buzzer: Part from https://www.nutsvolts.com/magazine/article/november2012_SmileysWorkshop modified to be .3 in spacing to match the adafruit buzzer 5V breadboard friendly part.
  HLK-5M05: AC-DC 220V to 5V Step-Down Power Supply Module
